# Fritzing sketch finalProject2 (saved by Fritzing 0.9.1b)
breadboards: 1

parts:
  Arduino = Arduino Uno (Rev3) - ICSP
  LIDAR-Lite = LIDAR-Lite
  J2 = Basic Servo
  R1 = Resistor [tolerance=±5% resistance=2.2k package="0603 [SMD]"]
  U1 = LIPO-2000mAh [package=lipo-2000]
  J1 = Basic Servo
  R2 = Resistor [tolerance=±5% resistance=2.2k package="0603 [SMD]"]

nets:
  N1: Arduino.A4/SDA, LIDAR-Lite.connector6
  N2: Arduino.A5/SCL, LIDAR-Lite.connector5
  GND: Arduino.GND, LIDAR-Lite.connector7, J2.gnd, U1.-, J1.gnd
  N3: Arduino.D9_PWM, J2.pulse
  N4: Arduino.D2, R1.Pin_1, R2.Pin_1
  N5: Arduino.D3_PWM, LIDAR-Lite.connector2, R1.Pin_0, R2.Pin_0
  N6: Arduino.D4, LIDAR-Lite.connector1
  N7: Arduino.D7, J1.pulse
  VCC: LIDAR-Lite.connector0, J2.vcc, U1.+, J1.vcc
